// Logisim project s-mips.circ as structural Verilog
module S_MIPS_Board (
  input  DESHABILITAR_DISPATCHER,
  output halt
);

  wire button_1_out, CLK, CS, d_ff_1_q, LCLR, LoadRAM, LoadRAMOn, LW, R_R_W, R_W, ram_dispatcher_1_finished,
       RCS, Reset_out, RST, TTY_EN;
  wire [2:0] KDB;
  wire [3:0] LMask, Mask, ram_1_read_time, ram_1_write_time, RMask;
  wire [6:0] KDB_DATA, TTY_DATA;
  wire [15:0] Addr, LAddr, RAddr;
  wire [31:0] I0, I1, I2, I3, LData, ram_1_data_out_0, ram_1_data_out_1, ram_1_data_out_2, ram_1_data_out_3,
       RI0, RI1, RI2, RI3;

  TTY #(.rows(25), .cols(80)) tty_1 (.data(TTY_DATA), .clk(CLK), .we(TTY_EN), .clr(RST));
  not not_1 (LoadRAMOn, ram_dispatcher_1_finished);
  RAM_Dispatcher ram_dispatcher_1 (
    .WriteTime(ram_1_write_time), .Clock(CLK), .Data(LData), .Address(LAddr), .Mask(LMask),
    .Finished(ram_dispatcher_1_finished), .Write(LW), .CLR(LCLR));
  Keyboard #(.buflen(64)) keyboard_1 (.clk(CLK), .re(KDB[0]), .avail(KDB[2]), .data(KDB_DATA));  // open: clr
  RAM ram_1 (
    .Address(RAddr), .Data_Out_0(ram_1_data_out_0), .Data_Out_1(ram_1_data_out_1),
    .Data_Out_2(ram_1_data_out_2), .Data_Out_3(ram_1_data_out_3), .Data_In_0(RI0), .Data_In_1(RI1),
    .Data_In_2(RI2), .Data_In_3(RI3), .Mask(RMask), .nRead_Write(R_R_W), .Chip_Select(RCS),
    .Read_Time(ram_1_read_time), .Reset(button_1_out), .Write_Time(ram_1_write_time));
  Button button_1 (.out(button_1_out));
  D_Flip_Flop d_ff_1 (.clk(CLK), .D(1'b1), .Q(d_ff_1_q), .reset(Reset_out));  // open: Qn, preset, en
  Button Reset (.out(Reset_out));
  S_MIPS s_mips_1 (
    .Kbd_Enable(KDB[0]), .Address(Addr), .Kbd_Clear(KDB[1]), .Kbd_Available(KDB[2]), .RAM_In_0(I0),
    .Kbd_ASCII_Data(KDB_DATA), .RAM_In_1(I1), .TTY_Enable(TTY_EN), .RAM_In_2(I2), .RAM_In_3(I3),
    .TTY_ASCII_Data(TTY_DATA), .Reset(RST), .RAM_Out_0(ram_1_data_out_0), .Clock(CLK),
    .RAM_Out_1(ram_1_data_out_1), .Stop(halt), .RAM_Out_2(ram_1_data_out_2), .RAM_Out_3(ram_1_data_out_3),
    .Mask(Mask), .Read_Time(ram_1_read_time), .Write_Time(ram_1_write_time), .nRead_Write(R_W),
    .Chip_Select(CS));
  D_Flip_Flop d_ff_2 (.clk(CLK), .D(d_ff_1_q), .Qn(LCLR), .reset(Reset_out));  // open: Q, preset, en
  or or_1 (RST, LCLR, LoadRAM);
  Clock clock_1 (.out(CLK));
  Multiplexer #(.width(32), .enable("false")) multiplexer_1 (.in0(I0), .in1(LData), .out(RI0), .sel(LoadRAM));
  Multiplexer #(.width(32), .enable("false")) multiplexer_2 (.in0(I1), .in1(LData), .out(RI1), .sel(LoadRAM));
  Multiplexer #(.width(32), .enable("false")) multiplexer_3 (.in0(I2), .in1(LData), .out(RI2), .sel(LoadRAM));
  Multiplexer #(.width(32), .enable("false")) multiplexer_4 (.in0(I3), .in1(LData), .out(RI3), .sel(LoadRAM));
  and and_1 (LoadRAM, ~DESHABILITAR_DISPATCHER, LoadRAMOn);  // AND_Gate
  Multiplexer #(.width(16), .enable("false")) multiplexer_5 (.in0(Addr), .in1(LAddr), .out(RAddr), .sel(LoadRAM));
  Multiplexer #(.width(4), .enable("false")) multiplexer_6 (.in0(Mask), .in1(LMask), .out(RMask), .sel(LoadRAM));
  Multiplexer #(.enable("false")) multiplexer_7 (.in0(CS), .in1(LW), .out(RCS), .sel(LoadRAM));
  Multiplexer #(.enable("false")) multiplexer_8 (.in0(R_W), .in1(LW), .out(R_R_W), .sel(LoadRAM));

  // Notes on the sheet:
  //   NO MODIFICAR
  //   Keyboard
endmodule

module RAM (
  input  [15:0] Address,
  input  [31:0] Data_In_0,
  input  [31:0] Data_In_1,
  input  [31:0] Data_In_2,
  input  [31:0] Data_In_3,
  input  [3:0] Mask,
  input  nRead_Write,
  input  Chip_Select,
  input  Reset,
  output [31:0] Data_Out_0,
  output [31:0] Data_Out_1,
  output [31:0] Data_Out_2,
  output [31:0] Data_Out_3,
  output [3:0] Read_Time,
  output [3:0] Write_Time
);

  wire and_2_out, and_3_out, and_4_out, and_5_out, and_6_out, and_7_out, and_8_out, and_9_out, Changed, CLK,
       comparator_2_eq, comparator_3_eq, comparator_4_eq, comparator_5_eq, comparator_6_eq, Count,
       demultiplexer_3_out0, Idle, Idle_q, Load, Load0, Load1, nand_1_out, or_1_out, or_2_out, or_3_out,
       or_4_out, or_5_out, or_6_out, or_7_out, or_8_out, or_9_out, or_10_out, Proc_q, Update_Mem, Zero_Time;
  wire [3:0] counter_1_q, multiplexer_1_out, subtractor_1_out;
  wire [31:0] register_1_q, register_2_q, register_3_q, register_4_q, register_5_q;

  // Probe on 4'b0011
  // Probe on 4'b0010
  Multiplexer #(.width(4), .enable("false")) multiplexer_1 (
    .in0(4'b0011), .in1(4'b0010), .out(multiplexer_1_out), .sel(nRead_Write));
  or or_1 (or_1_out, Idle, Update_Mem);
  or or_2 (or_2_out, ~Chip_Select, Reset);  // OR_Gate
  Subtractor #(.width(4)) subtractor_1 (.a(multiplexer_1_out), .b(4'b0010), .out(subtractor_1_out));  // open: bin, bout
  Demultiplexer #(.enable("false")) demultiplexer_1 (.out0(Idle), .out1(Load0), .in(Idle_q), .sel(Changed));
  D_Flip_Flop u_Idle (.clk(CLK), .D(or_1_out), .Q(Idle_q), .preset(or_2_out));  // open: Qn, en, reset
  // Probe on counter_1_q
  Counter #(.width(4), .max('hf)) counter_1 (
    .load(Load), .D(subtractor_1_out), .count(Count), .Q(counter_1_q), .clk(CLK), .clr(or_3_out));  // open: carry
  or or_3 (or_3_out, ~Chip_Select, Reset);  // OR_Gate
  Comparator #(.width(4), .mode("unsigned")) comparator_1 (
    .a(4'b0000), .b(counter_1_q), .eq(Zero_Time));  // open: gt, lt
  or or_4 (or_4_out, Count, Load0, Load1);
  Register #(.width(32)) register_1 (.D(Data_In_0), .en(Chip_Select), .Q(register_1_q), .clk(CLK), .clr(or_5_out));
  or or_5 (or_5_out, ~Chip_Select, Reset);  // OR_Gate
  Register #(.width(32)) register_2 (.D(Data_In_1), .en(Chip_Select), .Q(register_2_q), .clk(CLK), .clr(or_6_out));
  or or_6 (or_6_out, ~Chip_Select, Reset);  // OR_Gate
  Register #(.width(32)) register_3 (.D(Data_In_2), .en(Chip_Select), .Q(register_3_q), .clk(CLK), .clr(or_7_out));
  or or_7 (or_7_out, ~Chip_Select, Reset);  // OR_Gate
  Register #(.width(32)) register_4 (.D(Data_In_3), .en(Chip_Select), .Q(register_4_q), .clk(CLK), .clr(or_8_out));
  or or_8 (or_8_out, ~Chip_Select, Reset);  // OR_Gate
  Register #(.width(32)) register_5 (
    .D({{11{1'b1}}, nRead_Write, Mask, Address}), .en(Chip_Select), .Q(register_5_q), .clk(CLK),
    .clr(or_9_out));
  or or_9 (or_9_out, ~Chip_Select, Reset);  // OR_Gate
  D_Flip_Flop Proc (.clk(CLK), .D(or_4_out), .Q(Proc_q), .reset(or_10_out));  // open: Qn, preset, en
  or or_10 (or_10_out, ~Chip_Select, Reset);  // OR_Gate
  Demultiplexer #(.enable("false")) demultiplexer_2 (
    .out0(Count), .out1(Update_Mem), .in(demultiplexer_3_out0), .sel(Zero_Time));
  Demultiplexer #(.enable("false")) demultiplexer_3 (
    .out0(demultiplexer_3_out0), .out1(Load1), .in(Proc_q), .sel(Changed));
  Clock clock_1 (.out(CLK));
  Comparator #(.width(32)) comparator_2 (.a(register_1_q), .b(Data_In_0), .eq(comparator_2_eq));  // open: gt, lt
  Comparator #(.width(32)) comparator_3 (.a(register_2_q), .b(Data_In_1), .eq(comparator_3_eq));  // open: gt, lt
  Comparator #(.width(32)) comparator_4 (.a(register_3_q), .b(Data_In_2), .eq(comparator_4_eq));  // open: gt, lt
  Comparator #(.width(32)) comparator_5 (.a(register_4_q), .b(Data_In_3), .eq(comparator_5_eq));  // open: gt, lt
  Comparator #(.width(32)) comparator_6 (
    .a(register_5_q), .b({{11{1'b1}}, nRead_Write, Mask, Address}), .eq(comparator_6_eq));  // open: gt, lt
  nand nand_1 (nand_1_out, comparator_6_eq, comparator_2_eq, comparator_3_eq, comparator_4_eq, comparator_5_eq);
  and and_1 (Changed, nand_1_out, Chip_Select);
  or or_11 (Load, Count, Load1, Load0);
  and and_2 (and_2_out, Mask[0], Update_Mem, nRead_Write);
  and and_3 (and_3_out, Mask[1], Update_Mem, nRead_Write);
  and and_4 (and_4_out, Mask[2], Update_Mem, nRead_Write);
  and and_5 (and_5_out, Mask[3], Update_Mem, nRead_Write);
  RAM_part #(.addrWidth(16), .dataWidth(32), .bus("separate")) ram_1 (
    .addr(Address), .din(Data_In_0), .data(Data_Out_0), .str(and_2_out), .sel(Chip_Select), .clk(CLK),
    .ld(and_6_out), .clr(Reset));
  and and_6 (and_6_out, ~nRead_Write, Idle);  // AND_Gate
  RAM_part #(.addrWidth(16), .dataWidth(32), .bus("separate")) ram_2 (
    .addr(Address), .din(Data_In_1), .data(Data_Out_1), .str(and_3_out), .sel(Chip_Select), .clk(CLK),
    .ld(and_7_out), .clr(Reset));
  and and_7 (and_7_out, ~nRead_Write, Idle);  // AND_Gate
  RAM_part #(.addrWidth(16), .dataWidth(32), .bus("separate")) ram_3 (
    .addr(Address), .din(Data_In_2), .data(Data_Out_2), .str(and_4_out), .sel(Chip_Select), .clk(CLK),
    .ld(and_8_out), .clr(Reset));
  and and_8 (and_8_out, ~nRead_Write, Idle);  // AND_Gate
  RAM_part #(.addrWidth(16), .dataWidth(32), .bus("separate")) ram_4 (
    .addr(Address), .din(Data_In_3), .data(Data_Out_3), .str(and_5_out), .sel(Chip_Select), .clk(CLK),
    .ld(and_9_out), .clr(Reset));
  and and_9 (and_9_out, ~nRead_Write, Idle);  // AND_Gate

  assign Read_Time = 4'b0011;
  assign Write_Time = 4'b0010;

  // Other names for the same wires on the sheet: M0 = Mask[0]; M1 = Mask[1]; M2 = Mask[2]; M3 = Mask[3];
  //   RW = nRead_Write; CLR = Reset; CS = Chip_Select; Load2 = Count

  // Notes on the sheet:
  //   NO MODIFICAR
  //   excepto quizás los valores RT y WT
  //   BANK0
  //   BANK1
  //   BANK2
  //   BANK3
endmodule

module S_MIPS (
  input  Kbd_Available,
  input  [6:0] Kbd_ASCII_Data,
  input  [31:0] RAM_Out_0,
  input  [31:0] RAM_Out_1,
  input  Reset,
  input  [31:0] RAM_Out_2,
  input  Clock,
  input  [31:0] RAM_Out_3,
  input  [3:0] Read_Time,
  input  [3:0] Write_Time,
  output Kbd_Enable,
  output [15:0] Address,
  output Kbd_Clear,
  output TTY_Enable,
  output [6:0] TTY_ASCII_Data,
  output Stop,
  output [31:0] RAM_In_0,
  output [31:0] RAM_In_1,
  output [31:0] RAM_In_2,
  output [31:0] RAM_In_3,
  output [3:0] Mask,
  output nRead_Write,
  output Chip_Select
);

  wire Da_sel, Data_Sel, Hi_Lo, IR_Ld, Ld_Pc, Ld_RF, Ld_SP, RAM_Ready, RI_Start, RI_Write, Selector_A;
  wire [1:0] Addr_Sel, Bank, Pc_sel, Selector_B;
  wire [2:0] ALUsel, Branch_Flag, Di_sel;
  wire [5:0] FuncCode, OpCode;
  wire [31:0] Address_t, littleendianswap_1_output, RAM_Data, To_RAM;

  DataPath_2 datapath_1 (
    .RAM_out(RAM_Data), .Address(Address_t), .DAS(Da_sel), .DOS(Data_Sel), .AS(Selector_A), .BS(Selector_B),
    .BCS(Pc_sel), .Data_Out(To_RAM), .AddrS(Addr_Sel), .DIS(Di_sel), .ALUS(ALUsel), .FlagS(Branch_Flag),
    .OpCode(OpCode), .IM_R_W(IR_Ld), .FuncCode(FuncCode), .PC_R_W(Ld_Pc), .LH_R_W(Hi_Lo),
    .tty_out(TTY_ASCII_Data), .RF_R_W(Ld_RF), .SP_R_W(Ld_SP), .Clk(Clock), .KBD_Data(Kbd_ASCII_Data),
    .RST(Reset), .KBD_Avail(Kbd_Available));
  Control_Unit control_unit_1 (
    .in_1(OpCode), .in_2(FuncCode), .in_3(Clock), .in_5(Reset), .in_4(RAM_Ready), .out_6(Branch_Flag),
    .out_12(Selector_A), .out_7(ALUsel), .out_10(Di_sel), .out_14(Addr_Sel), .out_17(Data_Sel),
    .out_19(Selector_B), .out_21(Pc_sel), .out_23(Da_sel), .out_8(Hi_Lo), .out_9(RI_Write), .out_11(Ld_RF),
    .out_13(TTY_Enable), .out_15(Ld_Pc), .out_16(RI_Start), .out_18(Kbd_Enable), .out_20(Ld_SP),
    .out_22(Stop), .out_24(IR_Ld));
  LittleEndianSwap littleendianswap_1 (.Input(To_RAM), .Output(littleendianswap_1_output));
  Demultiplexer #(.select(2), .width(32), .enable("false")) demultiplexer_1 (
    .out0(RAM_In_0), .out1(RAM_In_1), .out2(RAM_In_2), .out3(RAM_In_3), .in(littleendianswap_1_output),
    .sel(Bank));
  RamManager rammanager_1 (
    .Addres_In(Address_t), .Ram_out_0(RAM_Out_0), .Ram_out_1(RAM_Out_1), .Ram_out_2(RAM_Out_2),
    .Ram_out_3(RAM_Out_3), .Read_Time(Read_Time), .Clk(Clock), .Rst(Reset), .Write_Time(Write_Time),
    .Start(RI_Start), .R_W(RI_Write), .From_RAM(RAM_Data), .Mask(Mask), .ADDR(Address), .RAMReady(RAM_Ready),
    .Chip_Select(Chip_Select), .RAM_Write(nRead_Write), .Bank(Bank));

  // Other names for the same wires on the sheet: CLK = Clock; CLR = Reset; CS = Chip_Select;
  //   KBD_AVAIL = Kbd_Available; KBD_CLR = Kbd_Clear; KBD_DATA[6:0] = Kbd_ASCII_Data; RAM_A[15:0] = Address;
  //   RAM_INPUT_0[31:0] = RAM_In_0; RAM_INPUT_1[31:0] = RAM_In_1; RAM_INPUT_2[31:0] = RAM_In_2;
  //   RAM_INPUT_3[31:0] = RAM_In_3; RAM_MASK[3:0] = Mask; RAM_OUTPUT_0[31:0] = RAM_Out_0;
  //   RAM_OUTPUT_1[31:0] = RAM_Out_1; RAM_OUTPUT_2[31:0] = RAM_Out_2; RAM_OUTPUT_3[31:0] = RAM_Out_3;
  //   RW = nRead_Write; TTY_DATA[6:0] = TTY_ASCII_Data

  // Notes on the sheet:
  //   RAM ADDRESS
  //   DATA FROM RAM
  //   DATA TO RAM
  //   DATA WRITE MASK
  //   RAM TIMING
  //   RAM CONTROL
  //   KEYBOARD
  //   TTY
  //   SEQUENCING
endmodule

module RAM_Dispatcher (
  input  [3:0] WriteTime,
  input  Clock,
  input  CLR,
  output [31:0] Data,
  output [15:0] Address,
  output [3:0] Mask,
  output Finished,
  output Write
);

  wire demultiplexer_2_out1, demultiplexer_3_out1, End, IDLE_q, IncAddr, Load, or_1_out, or_2_out, While_q,
       WriteEnd;
  wire [3:0] counter_1_q;
  wire [31:0] CurrentAddress_q;

  Counter #(.width(32), .max('hffffffff)) CurrentAddress (
    .count(IncAddr), .Q({CurrentAddress_q[31:18], Address, CurrentAddress_q[1:0]}), .clk(Clock), .clr(CLR));  // open: load, D, carry
  or or_1 (or_1_out, IncAddr, demultiplexer_3_out1, Finished);
  D_Flip_Flop IDLE (.clk(Clock), .D(or_1_out), .Q(IDLE_q), .preset(CLR));  // open: Qn, en, reset
  Demultiplexer #(.enable("false")) demultiplexer_1 (.out0(Load), .out1(Finished), .in(IDLE_q), .sel(End));
  D_Flip_Flop While (.clk(Clock), .D(or_2_out), .Q(While_q), .reset(CLR));  // open: Qn, preset, en
  or or_2 (or_2_out, Write, Load);
  RAM_part #(.addrWidth(18), .dataWidth(32)) ram_1 (
    .addr({Address, CurrentAddress_q[1:0]}), .data(Data), .clk(Clock));  // open: sel, ld, clr
  Demultiplexer #(.enable("false")) demultiplexer_2 (
    .out0(Write), .out1(demultiplexer_2_out1), .in(While_q), .sel(WriteEnd));
  Decoder #(.select(2)) decoder_1 (
    .out0(Mask[0]), .out1(Mask[1]), .out2(Mask[2]), .out3(Mask[3]), .sel(CurrentAddress_q[1:0]));  // open: en
  Demultiplexer #(.enable("false")) demultiplexer_3 (
    .out0(IncAddr), .out1(demultiplexer_3_out1), .in(demultiplexer_2_out1), .sel(End));
  Counter #(.width(4), .max('hf)) counter_1 (
    .load(Load), .D(WriteTime), .count(Write), .Q(counter_1_q), .clk(Clock));  // open: carry, clr
  Comparator #(.width(32)) comparator_1 (.a(Data), .b({32{1'b1}}), .eq(End));  // open: gt, lt
  Comparator #(.width(4)) comparator_2 (.a(4'b0000), .b(counter_1_q), .eq(WriteEnd));  // open: gt, lt

  // Other names for the same wires on the sheet: CLK = Clock; Count = Write; WT[3:0] = WriteTime
endmodule

module DataPath_2 (
  input  [31:0] RAM_out,
  input  DAS,
  input  DOS,
  input  AS,
  input  [1:0] BS,
  input  [1:0] BCS,
  input  [1:0] AddrS,
  input  [2:0] DIS,
  input  [2:0] ALUS,
  input  [2:0] FlagS,
  input  IM_R_W,
  input  PC_R_W,
  input  LH_R_W,
  input  RF_R_W,
  input  SP_R_W,
  input  Clk,
  input  [6:0] KBD_Data,
  input  RST,
  input  KBD_Avail,
  output [31:0] Address,
  output [31:0] Data_Out,
  output [5:0] OpCode,
  output [5:0] FuncCode,
  output [6:0] tty_out
);

  wire N, P, Z;
  wire [4:0] DA, RD, RS, RT;
  wire [25:0] Dest;
  wire [31:0] bit_extender_1_out, Hi, HiI, K, kbd_t, Lo, LoI, multiplexer_1_out, multiplexer_4_out,
       multiplexer_5_out, PC, PC_Out, R, rnd, RT_t, SP, UK;
  wire [31:7] RS_t;

  Multiplexer #(.select(3), .width(32), .enable("false")) multiplexer_1 (
    .in0(R), .in1(RAM_out), .in3(Lo), .in5(Hi), .in6(rnd), .in7(kbd_t), .out(multiplexer_1_out), .sel(DIS));  // open: in2, in4
  Multiplexer #(.width(5), .enable("false")) multiplexer_2 (.in0(RD), .in1(RT), .out(DA), .sel(DAS));
  InstructionSplitter instructionsplitter_1 (
    .Op(OpCode), .Func__Code(FuncCode), .Destino(Dest), .Inst(RAM_out), .RS(RS), .IM_R_W(IM_R_W), .RT(RT),
    .RD(RD), .Clk(Clk), .Rst(RST), .Sign_Const(K), .Unsgn_Const(UK));
  assign bit_extender_1_out = {{25{1'b0}}, KBD_Data};  // Bit_Extender bit_extender_1
  // RegisterFile registerfile_1: pin names not known; wires that end beside it: multiplexer_1_out, RF_R_W, RS, RT, DA, R, SP_R_W, Clk, RST, LoI, HiI, Lo, LH_R_W, Hi, {RS_t, tty_out}, SP, RT_t
  Multiplexer #(.width(32), .enable("false")) multiplexer_3 (
    .in0(bit_extender_1_out), .in1({32{1'b1}}), .out(kbd_t), .sel(KBD_Avail));
  Random #(.width(32)) random_1 (.clk(Clk), .out(rnd));  // open: next, clr
  Branch_Control branch_control_1 (
    .PC_in(PC), .BCSel(BCS), .FlagS(FlagS), .PC_out(PC_Out), .K(K), .Destino(Dest),
    .Register({RS_t, tty_out}), .Z(Z), .N(N), .P(P));
  Multiplexer #(.width(32), .enable("false")) multiplexer_4 (
    .in0({RS_t, tty_out}), .in1(SP), .out(multiplexer_4_out), .sel(AS));
  Multiplexer #(.select(2), .width(32), .enable("false")) multiplexer_5 (
    .in0(RT_t), .in1(K), .in2(UK), .in3(32'h4), .out(multiplexer_5_out), .sel(BS));
  ProgramCounter programcounter_1 (.In(PC_Out), .En_PC(PC_R_W), .clock(Clk), .Output(PC), .Reset(RST));
  ALU alu_1 (
    .R(R), .A(multiplexer_4_out), .Positive(P), .Zero(Z), .Negative(N), .B(multiplexer_5_out), .Lo(HiI),
    .S(ALUS), .Hi(LoI));
  Multiplexer #(.width(32), .enable("false")) multiplexer_6 (
    .in0(RT_t), .in1({RS_t, tty_out}), .out(Data_Out), .sel(DOS));
  Multiplexer #(.select(2), .width(32), .enable("false")) multiplexer_7 (
    .in0(PC), .in1(R), .in2(SP), .out(Address), .sel(AddrS));  // open: in3

  // Other names for the same wires on the sheet: Func[5:0] = FuncCode; IM_RW = IM_R_W; KBD = KBD_Avail;
  //   LH_RW = LH_R_W; OP[5:0] = OpCode; PC_RW = PC_R_W; RAM[31:0] = RAM_out; RF_RW = RF_R_W; RS_t[6:0] = tty_out;
  //   SP_RW = SP_R_W

  // Notes on the sheet:
  //   Selectors
  //   Loads
endmodule

module ALU (
  input  [31:0] A,
  input  [31:0] B,
  input  [2:0] S,
  output [31:0] R,
  output Positive,
  output Zero,
  output Negative,
  output [31:0] Lo,
  output [31:0] Hi
);

  wire comparator_1_lt, comparator_2_lt;
  wire [31:0] And, Diff, HiDiv, HiDivu, HiMult, HiMulu, LoDiv, LoDivu, LoMult, LoMulu, Nor, Or, slt, sltu,
       Sum, Xor;

  Adder #(.width(32)) adder_1 (.a(A), .b(B), .out(Sum));  // open: cin, cout
  Subtractor #(.width(32)) subtractor_1 (.a(A), .b(B), .out(Diff));  // open: bin, bout
  assign And = A & B;  // AND_Gate and_1, 32 bits wide
  assign Or = A | B;  // OR_Gate or_1, 32 bits wide
  assign Nor = ~Or;  // NOT_Gate not_1, 32 bits wide
  assign Xor = A ^ B;  // XOR_Gate xor_1, 32 bits wide
  SignedMultiplier signedmultiplier_1 (.A(A), .B(B), .Low(LoMult), .High(HiMult));
  Multiplier #(.width(32)) multiplier_1 (.a(A), .b(B), .out(LoMulu), .cout(HiMulu));  // open: cin
  Comparator #(.width(32)) comparator_1 (.a(A), .b(B), .lt(comparator_1_lt));  // open: gt, eq
  Comparator #(.width(32), .mode("unsigned")) comparator_2 (.a(A), .b(B), .lt(comparator_2_lt));  // open: gt, eq
  SignedDivider signeddivider_1 (.A(A), .Low(LoDiv), .B(B), .High(HiDiv));
  Divider #(.width(32)) divider_1 (.a(A), .b(B), .out(LoDivu), .rem(HiDivu));  // open: upper
  assign slt = {{31{1'b0}}, comparator_1_lt};  // Bit_Extender bit_extender_1
  assign sltu = {{31{1'b0}}, comparator_2_lt};  // Bit_Extender bit_extender_2
  Multiplexer #(.select(3), .width(32), .enable("false")) multiplexer_1 (
    .in0(Sum), .in1(Diff), .in2(And), .in3(Or), .in4(Nor), .in5(Xor), .in6(slt), .in7(sltu), .out(R), .sel(S));
  Multiplexer #(.select(2), .width(32), .enable("false")) multiplexer_2 (
    .in0(LoMult), .in1(LoMulu), .in2(LoDiv), .in3(LoDivu), .out(Lo), .sel(S[1:0]));
  Multiplexer #(.select(2), .width(32), .enable("false")) multiplexer_3 (
    .in0(HiMult), .in1(HiMulu), .in2(HiDiv), .in3(HiDivu), .out(Hi), .sel(S[1:0]));
  Comparator #(.width(32)) comparator_3 (.a(R), .b({32{1'b0}}), .gt(Positive), .eq(Zero), .lt(Negative));

  // Other names for the same wires on the sheet: LoHi_S[1:0] = S[1:0]

  // Notes on the sheet:
  //   Inputs
  //   ALU
  //   Arithmetic Ops
  //   Logic Ops
  //   Unisgned
  //   Outputs
endmodule

module SignedMultiplier (
  input  [31:0] A,
  input  [31:0] B,
  output [31:0] Low,
  output [31:0] High
);

  wire adder_1_cout, Sign_A, Sign_B, Sign_R;
  wire [31:0] minus_High, minus_Low, not_1_out, not_2_out, plus_High, plus_Low, sign_1_out, sign_2_out;

  Sign sign_1 (.In(A), .Out(sign_1_out), .Sign(Sign_A));
  Sign sign_2 (.In(B), .Out(sign_2_out), .Sign(Sign_B));
  xor xor_1 (Sign_R, Sign_A, Sign_B);
  Multiplier #(.width(32)) multiplier_1 (
    .a(sign_1_out), .b(sign_2_out), .out(plus_Low), .cout(plus_High));  // open: cin
  assign not_1_out = ~plus_Low;  // NOT_Gate not_1, 32 bits wide
  assign not_2_out = ~plus_High;  // NOT_Gate not_2, 32 bits wide
  Adder #(.width(32)) adder_1 (.a(not_1_out), .b(32'h1), .out(minus_Low), .cout(adder_1_cout));  // open: cin
  Adder #(.width(32)) adder_2 (.a(not_2_out), .b({32{1'b0}}), .out(minus_High), .cin(adder_1_cout));  // open: cout
  Multiplexer #(.width(32), .enable("false")) multiplexer_1 (.in0(plus_Low), .in1(minus_Low), .out(Low), .sel(Sign_R));
  Multiplexer #(.width(32), .enable("false")) multiplexer_2 (
    .in0(plus_High), .in1(minus_High), .out(High), .sel(Sign_R));

  // Notes on the sheet:
  //   Final Sign
  //   Negator
  //   Outputs
endmodule

module SignedDivider (
  input  [31:0] A,
  input  [31:0] B,
  output [31:0] Low,
  output [31:0] High
);

  wire Sign_A, Sign_B, Sign_Quo;
  wire [31:0] minus_Quo, minus_Rem, plus_Quo, plus_Rem, sign_1_out, sign_2_out;

  Sign sign_1 (.In(A), .Out(sign_1_out), .Sign(Sign_A));
  Sign sign_2 (.In(B), .Out(sign_2_out), .Sign(Sign_B));
  xor xor_1 (Sign_Quo, Sign_A, Sign_B);
  Divider #(.width(32)) divider_1 (.a(sign_1_out), .b(sign_2_out), .out(plus_Quo), .rem(plus_Rem));  // open: upper
  Negator #(.width(32)) negator_1 (.in(plus_Quo), .out(minus_Quo));
  Negator #(.width(32)) negator_2 (.in(plus_Rem), .out(minus_Rem));
  Multiplexer #(.width(32), .enable("false")) multiplexer_1 (
    .in0(plus_Quo), .in1(minus_Quo), .out(Low), .sel(Sign_Quo));
  Multiplexer #(.width(32), .enable("false")) multiplexer_2 (.in0(plus_Rem), .in1(minus_Rem), .out(High), .sel(Sign_A));

  // Notes on the sheet:
  //   Quotient Sign
  //   Negator
  //   Outputs
endmodule

module Sign (
  input  [31:0] In,
  output [31:0] Out,
  output Sign
);

  wire [31:0] negator_1_out;

  BitSelector #(.width(32)) bitselector_1 (.in(In), .out(Sign), .sel({5{1'b1}}));
  Multiplexer #(.width(32), .enable("false")) multiplexer_1 (.in0(In), .in1(negator_1_out), .out(Out), .sel(Sign));
  Negator #(.width(32)) negator_1 (.in(In), .out(negator_1_out));

  // Notes on the sheet:
  //   Absolute Value and Sign
endmodule

module ProgramCounter (
  input  [31:0] In,
  input  En_PC,
  input  clock,
  input  Reset,
  output [31:0] Output
);

  Register #(.width(32), .trigger("falling")) register_1 (.D(In), .en(En_PC), .Q(Output), .clk(clock), .clr(Reset));

  // Other names for the same wires on the sheet: clk = clock; En = En_PC; Ou[31:0] = Output; rst = Reset

  // Notes on the sheet:
  //   Inputs:
  //   Register:
  //   Program Counter:
  //   Output:
endmodule

module InstructionSplitter (
  input  [31:0] Inst,
  input  Clk,
  input  Rst,
  input  IM_R_W,
  output [5:0] Op,
  output [5:0] Func__Code,
  output [25:0] Destino,
  output [4:0] RS,
  output [4:0] RT,
  output [4:0] RD,
  output [31:0] Sign_Const,
  output [31:0] Unsgn_Const
);

  Register #(.width(32), .trigger("falling")) register_1 (
    .D(Inst), .en(IM_R_W), .Q({Op, Destino}), .clk(Clk), .clr(Rst));
  assign Sign_Const = {{16{Destino[15]}}, Destino[15:0]};  // Bit_Extender bit_extender_1
  assign Unsgn_Const = {{16{1'b0}}, Destino[15:0]};  // Bit_Extender bit_extender_2

  assign Func__Code = Destino[5:0];
  assign RD = Destino[15:11];
  assign RS = Destino[25:21];
  assign RT = Destino[20:16];

  // Other names for the same wires on the sheet: Destin[25:0] = Destino; FC[5:0] = Destino[5:0];
  //   K[15:0] = Destino[15:0]

  // Notes on the sheet:
  //   Inputs
  //   Outputs
endmodule

// RF
module RegisterFile (
  input  [4:0] DA,
  input  [31:0] DI,
  input  R_W,
  input  [4:0] SA,
  input  [4:0] SB,
  input  Clk,
  input  Reset,
  input  [31:0] Lo,
  input  [31:0] Hi,
  input  LH_RW,
  input  [31:0] SP,
  input  SP_RW,
  output [31:0] Data_A,
  output [31:0] Stack_Pointer,
  output [31:0] Data_B,
  output [31:0] Lo_2,
  output [31:0] Hi_2
);

  wire L1, L2, L3, L4, L5, L6, L7, L8, L9, L10, L11, L12, L13, L14, L15, L16, L17, L18, L19, L20, L21, L22,
       L23, L24, L25, L26, L27, L28, L29, L30, L31, SPW, undriven, undriven_2, undriven_3, undriven_4,
       undriven_5, undriven_6, undriven_7, undriven_8, undriven_9, undriven_10, undriven_11, undriven_12;
  wire [31:0] R1, R2, R3, R4, R5, R6, R7, R8, R9, R10, R11, R12, R13, R14, R15, R16, R17, R18, R19, R20, R21,
       R22, R23, R24, R25, R26, R27, R28, R29, R30;

  Register #(.width(32), .trigger("falling")) register_1 (.D(Lo), .en(LH_RW), .Q(Lo_2), .clk(Clk), .clr(Reset));
  Register #(.width(32), .trigger("falling")) register_2 (.D(Hi), .en(LH_RW), .Q(Hi_2), .clk(Clk), .clr(Reset));
  Decoder #(.select(5), .disabled(0)) decoder_1 (
    .out1(L1), .out2(L2), .out3(L3), .out4(L4), .out5(L5), .out6(L6), .out7(L7), .out8(L8), .out9(L9),
    .out10(L10), .out11(L11), .out12(L12), .out13(L13), .out14(L14), .out15(L15), .out16(L16), .out17(L17),
    .out18(L18), .out19(L19), .out20(L20), .out21(L21), .out22(L22), .out23(L23), .out24(L24), .out25(L25),
    .out26(L26), .out27(L27), .out28(L28), .out29(L29), .out30(L30), .out31(L31), .sel(DA), .en(R_W));  // open: out0
  or or_1 (SPW, SP_RW, L31);
  Register #(.width(32), .trigger("falling")) register_3 (.D(DI), .en(L1), .Q(R1), .clk(Clk), .clr(Reset));
  Register #(.width(32), .trigger("falling")) register_4 (.D(DI), .en(L4), .Q(R4), .clk(Clk), .clr(Reset));
  Register #(.width(32), .trigger("falling")) register_5 (.D(DI), .en(L5), .Q(R5), .clk(Clk), .clr(Reset));
  Register #(.width(32), .trigger("falling")) register_6 (.D(DI), .en(L6), .Q(R6), .clk(Clk), .clr(Reset));
  Register #(.width(32), .trigger("falling")) register_7 (.D(DI), .en(L7), .Q(R7), .clk(Clk), .clr(Reset));
  Register #(.width(32), .trigger("falling")) register_8 (.D(DI), .en(L2), .Q(R2), .clk(Clk), .clr(Reset));
  Register #(.width(32), .trigger("falling")) register_9 (.D(DI), .en(L3), .Q(R3), .clk(Clk), .clr(Reset));
  Register #(.width(32), .trigger("falling")) register_10 (.D(DI), .en(L8), .Q(R8), .clk(Clk), .clr(Reset));
  Register #(.width(32), .trigger("falling")) register_11 (.D(DI), .en(L9), .Q(R9), .clk(Clk), .clr(Reset));
  Register #(.width(32), .trigger("falling")) register_12 (.D(DI), .en(L11), .Q(R11), .clk(Clk), .clr(Reset));
  Register #(.width(32), .trigger("falling")) register_13 (.D(DI), .en(L12), .Q(R12), .clk(Clk), .clr(Reset));
  Register #(.width(32), .trigger("falling")) register_14 (.D(DI), .en(L13), .Q(R13), .clk(Clk), .clr(Reset));
  Register #(.width(32), .trigger("falling")) register_15 (.D(DI), .en(L14), .Q(R14), .clk(Clk), .clr(Reset));
  Register #(.width(32), .trigger("falling")) register_16 (.D(DI), .en(L15), .Q(R15), .clk(Clk), .clr(Reset));
  Register #(.width(32), .trigger("falling")) register_17 (.D(DI), .en(L10), .Q(R10), .clk(Clk), .clr(Reset));
  Register #(.width(32), .trigger("falling")) register_18 (.D(DI), .en(L16), .Q(R16), .clk(Clk), .clr(Reset));
  Register #(.width(32), .trigger("falling")) register_19 (.D(DI), .en(undriven), .Q(R17), .clk(Clk), .clr(Reset));
  Register #(.width(32), .trigger("falling")) register_20 (.D(DI), .en(undriven_2), .Q(R18), .clk(Clk), .clr(Reset));
  Register #(.width(32), .trigger("falling")) register_21 (.D(DI), .en(L19), .Q(R19), .clk(Clk), .clr(Reset));
  Register #(.width(32), .trigger("falling")) register_22 (.D(DI), .en(undriven_3), .Q(R20), .clk(Clk), .clr(Reset));
  Register #(.width(32), .trigger("falling")) register_23 (.D(DI), .en(L21), .Q(R21), .clk(Clk), .clr(Reset));
  Register #(.width(32), .trigger("falling")) register_24 (.D(DI), .en(undriven_4), .Q(R22), .clk(Clk), .clr(Reset));
  Register #(.width(32), .trigger("falling")) register_25 (.D(DI), .en(undriven_5), .Q(R23), .clk(Clk), .clr(Reset));
  Register #(.width(32), .trigger("falling")) register_26 (.D(DI), .en(L24), .Q(R24), .clk(Clk), .clr(Reset));
  Register #(.width(32), .trigger("falling")) register_27 (.D(DI), .en(undriven_6), .Q(R25), .clk(Clk), .clr(Reset));
  Register #(.width(32), .trigger("falling")) register_28 (.D(DI), .en(undriven_7), .Q(R26), .clk(Clk), .clr(Reset));
  Register #(.width(32), .trigger("falling")) register_29 (.D(DI), .en(undriven_8), .Q(R27), .clk(Clk), .clr(Reset));
  Register #(.width(32), .trigger("falling")) register_30 (.D(DI), .en(undriven_9), .Q(R28), .clk(Clk), .clr(Reset));
  Register #(.width(32), .trigger("falling")) register_31 (.D(DI), .en(undriven_10), .Q(R29), .clk(Clk), .clr(Reset));
  Register #(.width(32), .trigger("falling")) register_32 (.D(DI), .en(undriven_11), .Q(R30), .clk(Clk), .clr(Reset));
  Register #(.width(32), .trigger("falling")) register_33 (
    .D(SP), .en(undriven_12), .Q(Stack_Pointer), .clk(Clk), .clr(Reset));
  Multiplexer #(.select(5), .width(32), .enable("false")) multiplexer_1 (
    .in0({32{1'b0}}), .in1(R1), .in2(R2), .in3(R3), .in4(R4), .in5(R5), .in6(R6), .in7(R7), .in8(R8),
    .in9(R9), .in10(R10), .in11(R11), .in12(R12), .in13(R13), .in14(R14), .in15(R15), .in16(R16), .in17(R17),
    .in18(R18), .in19(R19), .in20(R20), .in21(R21), .in22(R22), .in23(R23), .in24(R24), .in25(R25),
    .in26(R26), .in27(R27), .in28(R28), .in29(R29), .in30(R30), .in31(Stack_Pointer), .out(Data_A), .sel(SA));
  Multiplexer #(.select(5), .width(32), .enable("false")) multiplexer_2 (
    .in0({32{1'b0}}), .in1(R1), .in2(R2), .in3(R3), .in4(R4), .in5(R5), .in6(R6), .in7(R7), .in8(R8),
    .in9(R9), .in10(R10), .in11(R11), .in12(R12), .in13(R13), .in14(R14), .in15(R15), .in16(R16), .in17(R17),
    .in18(R18), .in19(R19), .in20(R20), .in21(R21), .in22(R22), .in23(R23), .in24(R24), .in25(R25),
    .in26(R26), .in27(R27), .in28(R28), .in29(R29), .in30(R30), .in31(Stack_Pointer), .out(Data_B), .sel(SB));

  // Other names for the same wires on the sheet: Hi_t[31:0] = Hi_2; Lo_t[31:0] = Lo_2; LoHiRW = LH_RW; Rst = Reset;
  //   SP_t[31:0] = Stack_Pointer; SPIn[31:0] = SP

  // Notes on the sheet:
  //   Inputs
  //   Data Address
  //   Data In
  //   Read/Write
  //   Selector A
  //   Selector B
  //   Lo HIi R/W
  //   Lo
  //   Hi
  //   SP R/W
  //   SP
  //   Outputs
endmodule

// 1
module Branch_Control (
  input  [31:0] PC_in,
  input  [1:0] BCSel,
  input  [2:0] FlagS,
  input  [31:0] K,
  input  [25:0] Destino,
  input  [31:0] Register,
  input  Z,
  input  N,
  input  P,
  output [31:0] PC_out
);

  wire Flag, lez, neq;
  wire [31:0] adder_1_out, adder_2_out, multiplexer_2_out, shifter_1_out;

  not not_1 (neq, Z);
  Multiplexer #(.select(3), .enable("false")) multiplexer_1 (
    .in0(Z), .in1(lez), .in2(neq), .in6(N), .in7(P), .out(Flag), .sel(FlagS));  // open: in3, in4, in5
  not not_2 (lez, P);
  Adder #(.width(32)) adder_1 (.a(PC_in), .b(32'h4), .out(adder_1_out));  // open: cin, cout
  Shifter #(.width(32)) shifter_1 (.in(K), .\dist (5'b00010), .out(shifter_1_out));
  Adder #(.width(32)) adder_2 (.a(adder_1_out), .b(shifter_1_out), .out(adder_2_out));  // open: cin, cout
  Multiplexer #(.width(32), .enable("false")) multiplexer_2 (
    .in0(adder_1_out), .in1(adder_2_out), .out(multiplexer_2_out), .sel(Flag));
  Multiplexer #(.select(2), .width(32), .enable("false")) multiplexer_3 (
    .in0(adder_1_out), .in1(multiplexer_2_out), .in2(Register), .in3({PC_in[31:28], Destino, 2'b00}),
    .out(PC_out), .sel(BCSel));

  // Other names for the same wires on the sheet: BCS[1:0] = BCSel; eq = Z; FS[2:0] = FlagS; gtz = P; ltz = N;
  //   R[31:0] = Register

  // Notes on the sheet:
  //   Branch Control
endmodule

module Control_Unit (
  input  [5:0] in_1,
  input  [5:0] in_2,
  input  in_3,
  input  in_4,
  input  in_5,
  output [2:0] out_6,
  output [2:0] out_7,
  output out_8,
  output out_9,
  output [2:0] out_10,
  output out_11,
  output out_12,
  output out_13,
  output [1:0] out_14,
  output out_15,
  output out_16,
  output out_17,
  output out_18,
  output [1:0] out_19,
  output out_20,
  output [1:0] out_21,
  output out_22,
  output out_23,
  output out_24
);

  wire add, addi, \and , andi, beq, bgtz, blez, bltz, bne, d_ff_1_q, d_ff_2_q, demultiplexer_1_out0,
       demultiplexer_1_out1, demultiplexer_2_out0, div, divu, En_AL, En_B, En_I, En_S, En_Sp, En_W, EndS,
       Endw, halt_t, jmp, jr, kbd_t, Load_IM_q, lw, mfhi, mflo, mul, mulu, next, nop, \nor , not_1_out, \or ,
       or_11_out, or_15_out, ori, PCal, PCb, PCi, PCs, PCsp, PCw, pop, push, RamWs, RamWw, RFal, RfE, RFi,
       Rfs, Rfw, rnd, S_DAi, S_DAw, slt, slti, sltiu, sltu, StartRamF, StartRams, StartRamw, sub, sw, tty_t,
       Type_AL, Type_B, Type_I, Type_S, Type_Sp, Type_W, \xor , xori;
  wire [1:0] S_Adrs, S_Adrw, S_BCal, S_BCb, S_Bi, S_Bs, S_Bw;
  wire [2:0] S_ALUal, S_ALUb, S_ALUi, S_ALUs, S_Dial, S_DiE, S_Dis, S_Diw;

  or or_1 (Type_B, beq, bne, blez, bgtz, bltz, jmp);
  or or_2 (Type_AL, add, sub, \and , \or , \xor , \nor , slt, sltu, mul, mulu, div, divu, mfhi, mflo, jr, nop);
  DECODER decoder_1 (
    .in_1(in_1), .in_2(in_2), .nop(nop), .add(add), .sub(sub), .mult(mul), .mulu(mulu), .div(div),
    .divu(divu), .slt(slt), .sltu(sltu), .\and (\and ), .\or (\or ), .\xor (\xor ), .\nor (\nor ), .pop(pop),
    .push(push), .mfhi(mfhi), .mflo(mflo), .jr(jr), .addi(addi), .sltiu(sltiu), .slti(slti), .ori(ori),
    .andi(andi), .xori(xori), .lw(lw), .sw(sw), .beq(beq), .bne(bne), .blez(blez), .bgtz(bgtz), .bltz(bltz),
    .J(jmp), .halt(halt_t), .tty(tty_t), .rnd(rnd), .kbd(kbd_t));
  or or_3 (Type_I, addi, andi, ori, xori, slti, sltiu);
  or or_4 (Type_Sp, kbd_t, rnd, tty_t);
  or or_5 (Type_W, lw, sw);
  or or_6 (Type_S, pop, push);
  Demultiplexer #(.enable("false")) demultiplexer_1 (
    .out0(demultiplexer_1_out0), .out1(demultiplexer_1_out1), .in(d_ff_1_q), .sel(not_1_out));
  D_Flip_Flop d_ff_1 (.clk(in_3), .D(demultiplexer_1_out0), .Q(d_ff_1_q), .preset(in_5));  // open: Qn, en, reset
  assign out_7 = S_ALUal | S_ALUi | S_ALUb | S_ALUs;  // OR_Gate or_7, 3 bits wide
  assign out_19 = S_Bs | S_Bi | S_Bw;  // OR_Gate or_8, 2 bits wide
  assign out_21 = S_BCb | S_BCal;  // OR_Gate or_9, 2 bits wide
  not not_1 (not_1_out, in_5);
  TYPE_AL type_al_1 (
    .Inputs(En_AL), .in_2(add), .in_3(sub), .in_4(\and ), .in_5(\or ), .in_6(\xor ), .in_7(\nor ),
    .in_8(slt), .in_9(sltu), .in_10(mul), .in_11(mulu), .in_12(div), .in_13(divu), .in_14(mfhi),
    .in_15(mflo), .in_16(jr), .in_17(nop), .out_18(RFal), .out_19(PCal), .out_20(S_ALUal), .out_21(out_8),
    .out_22(S_Dial), .out_23(S_BCal));
  TYPE_STACK type_stack_1 (
    .out_6(StartRams), .out_7(Rfs), .out_8(out_12), .in_1(pop), .out_9(S_Adrs), .out_10(S_Bs), .in_2(push),
    .out_11(PCs), .in_3(En_S), .out_12(S_ALUs), .in_4(in_4), .out_13(out_20), .out_14(RamWs), .in_5(in_3),
    .out_15(out_17), .out_16(EndS), .out_17(S_Dis));
  or or_10 (StartRamF, next, demultiplexer_1_out1);
  or or_11 (or_11_out, StartRamF, d_ff_2_q);
  Demultiplexer #(.enable("false")) demultiplexer_2 (
    .out0(demultiplexer_2_out0), .out1(out_24), .in(or_11_out), .sel(in_4));
  D_Flip_Flop d_ff_2 (.clk(in_3), .D(demultiplexer_2_out0), .Q(d_ff_2_q));  // open: Qn, preset, en, reset
  assign out_10 = S_Dial | S_Dis | S_Diw | S_DiE;  // OR_Gate or_12, 3 bits wide
  assign out_14 = S_Adrs | S_Adrw;  // OR_Gate or_13, 2 bits wide
  or or_14 (out_23, S_DAi, S_DAw);
  D_Flip_Flop Load_IM (.clk(in_3), .D(out_24), .Q(Load_IM_q));  // open: Qn, preset, en, reset
  TYPE_INM type_inm_1 (
    .Inputs(En_I), .in_2(addi), .in_3(andi), .in_4(ori), .in_5(xori), .in_6(slti), .in_7(sltiu),
    .Outputs(S_Bi), .out_11(S_ALUi), .out_12(S_DAi), .out_9(PCi), .out_10(RFi));
  TYPE_WORD type_word_1 (
    .out_6(StartRamw), .Inputs(En_W), .out_7(RamWw), .out_8(S_DAw), .in_2(lw), .out_9(Rfw), .in_3(sw),
    .out_10(S_Diw), .in_4(in_3), .out_11(Endw), .in_5(in_4), .out_12(S_Bw), .out_13(S_Adrw), .out_14(PCw));
  D_Flip_Flop #(.trigger("high")) Halt (.clk(in_3), .D(or_15_out), .Q(out_22));  // open: Qn, preset, en, reset
  or or_15 (or_15_out, halt_t, out_22);
  or or_16 (out_9, RamWs, RamWw);
  or or_17 (out_16, StartRams, StartRamF, StartRamw);
  and and_1 (En_AL, Type_AL, Load_IM_q);
  and and_2 (En_I, Type_I, Load_IM_q);
  and and_3 (En_B, Type_B, Load_IM_q);
  and and_4 (En_W, Type_W, Load_IM_q);
  and and_5 (En_Sp, Type_Sp, Load_IM_q);
  and and_6 (En_S, Type_S, Load_IM_q);
  TYPE_BRANCH type_branch_1 (
    .out_8(PCb), .Inputs(En_B), .in_2(beq), .out_9(S_ALUb), .in_3(bne), .in_4(blez), .in_5(bgtz),
    .in_6(bltz), .in_7(jmp), .out_11(out_6), .out_10(S_BCb));
  TYPE_SPECIAL type_special_1 (
    .Inputs(En_Sp), .out_5(RfE), .in_2(kbd_t), .out_6(S_DiE), .in_3(rnd), .in_4(tty_t), .out_9(out_13),
    .out_8(PCsp), .out_7(out_18));
  or or_18 (out_11, RfE, RFal, RFi, Rfw, Rfs);
  or or_19 (out_15, PCal, PCi, PCs, PCsp, PCb, PCw);
  or or_20 (next, En_AL, En_I, En_Sp, En_B, Endw, EndS);

  // Other names for the same wires on the sheet: Clk = in_3; FunCode[5:0] = in_2; HALT = out_22; En_KBD = out_18;
  //   KBD = out_18; L_IM = out_24; L_LoHi = out_8; LH = out_8; OpCode[5:0] = in_1; PC = out_15; RamReady = in_4;
  //   RamW = out_9; Rf_Rw = out_11; S_Adr[1:0] = out_14; S_ALU[2:0] = out_7; S_A = out_12; S_As = out_12;
  //   S_B[1:0] = out_19; S_BC[1:0] = out_21; S_DA = out_23; S_Di[2:0] = out_10; S_DO = out_17; S_flag[2:0] = out_6;
  //   S_flags[2:0] = out_6; SP = out_20; SPs = out_20; start = in_5; StartRam = out_16; TTY = out_13; tty_En = out_13

  // Notes on the sheet:
  //   INPUTS
  //   DECODER
  //   Group
  //   IDLE
  //   Selectors:
  //   CONTROL UNIT FLOW 
  //   FETCH
  //   SWITCH
  //   Loads:
  //   OUTPUTS:
endmodule

module DECODER (
  input  [5:0] in_1,
  input  [5:0] in_2,
  output nop,
  output add,
  output sub,
  output mult,
  output mulu,
  output div,
  output divu,
  output slt,
  output sltu,
  output \and ,
  output \or ,
  output \xor ,
  output \nor ,
  output pop,
  output push,
  output mfhi,
  output mflo,
  output jr,
  output addi,
  output sltiu,
  output slti,
  output ori,
  output andi,
  output xori,
  output lw,
  output sw,
  output beq,
  output bne,
  output blez,
  output bgtz,
  output bltz,
  output J,
  output halt,
  output tty,
  output rnd,
  output kbd
);

  wire _00, _01, _10, _11, and_1_out, and_11_out, and_12_out, and_29_out, and_32_out, and_33_out, and_34_out,
       and_47_out, comparator_2_eq, Especial, I, or_1_out, R, R_00, R_01, R_10;

  Comparator #(.width(6)) comparator_1 (.a(in_1), .b(6'b000010), .eq(J));  // open: gt, lt
  Comparator #(.width(6)) comparator_2 (.a(in_1), .b({6{1'b0}}), .eq(comparator_2_eq));  // open: gt, lt
  or or_1 (or_1_out, comparator_2_eq, and_1_out);
  and and_1 (and_1_out, in_1[5], in_1[4], in_1[3]);
  and and_2 (Especial, and_1_out, in_1[2]);
  and and_3 (I, ~or_1_out, ~J);  // AND_Gate
  and and_4 (R, or_1_out, ~Especial);  // AND_Gate
  and and_5 (_10, ~in_1[0], I, in_1[1]);  // AND_Gate
  and and_6 (_11, in_1[0], I, in_1[1]);
  and and_7 (_01, in_1[0], I, ~in_1[1]);  // AND_Gate
  and and_8 (_00, ~in_1[0], I, ~in_1[1]);  // AND_Gate
  and and_9 (mflo, ~in_2[3], R_01, in_2[1]);  // AND_Gate
  and and_10 (mfhi, ~in_2[3], R_01, ~in_2[1]);  // AND_Gate
  and and_11 (and_11_out, in_2[3], R_01, ~in_2[1]);  // AND_Gate
  and and_12 (and_12_out, in_2[3], R_01, in_2[1]);
  and and_13 (R_00, ~in_2[4], R, ~in_2[5]);  // AND_Gate
  and and_14 (R_10, ~in_2[4], R, in_2[5]);  // AND_Gate
  and and_15 (R_01, in_2[4], R, ~in_2[5]);  // AND_Gate
  and and_16 (divu, and_12_out, in_2[0]);
  and and_17 (div, and_12_out, ~in_2[0]);  // AND_Gate
  and and_18 (mulu, and_11_out, in_2[0]);
  and and_19 (mult, and_11_out, ~in_2[0]);  // AND_Gate
  and and_20 (addi, ~in_1[2], _00, in_1[3]);  // AND_Gate
  and and_21 (andi, in_1[2], _00, in_1[3]);
  and and_22 (beq, in_1[2], _00, ~in_1[3]);  // AND_Gate
  and and_23 (sltiu, ~in_1[5], _11, in_1[3]);  // AND_Gate
  and and_24 (sw, in_1[5], _11, in_1[3]);
  and and_25 (lw, in_1[5], _11, ~in_1[3]);  // AND_Gate
  and and_26 (bgtz, ~in_1[5], _11, ~in_1[3]);  // AND_Gate
  and and_27 (jr, ~in_2[0], R_00, in_2[3]);  // AND_Gate
  and and_28 (push, in_2[0], R_00, ~in_2[3]);  // AND_Gate
  and and_29 (and_29_out, ~in_2[0], R_00, ~in_2[3]);  // AND_Gate
  and and_30 (pop, and_29_out, in_1[5]);
  and and_31 (nop, and_29_out, ~in_1[5]);  // AND_Gate
  and and_32 (and_32_out, ~in_2[3], R_10, ~in_2[2]);  // AND_Gate
  and and_33 (and_33_out, in_2[3], R_10, in_2[1]);
  and and_34 (and_34_out, ~in_2[3], R_10, in_2[2]);  // AND_Gate
  and and_35 (\xor , in_2[3], R_10, ~in_2[1]);  // AND_Gate
  and and_36 (slti, ~in_1[2], _10, in_1[3]);  // AND_Gate
  and and_37 (xori, in_1[2], _10, in_1[3]);
  and and_38 (blez, in_1[2], _10, ~in_1[3]);  // AND_Gate
  and and_39 (bne, in_1[2], _01, ~in_1[3]);  // AND_Gate
  and and_40 (ori, in_1[2], _01, in_1[3]);
  and and_41 (bltz, ~in_1[2], _01, ~in_1[3]);  // AND_Gate
  and and_42 (sub, in_2[1], and_32_out);
  and and_43 (add, ~in_2[1], and_32_out);  // AND_Gate
  and and_44 (sltu, and_33_out, in_2[0]);
  and and_45 (slt, ~in_2[0], and_33_out);  // AND_Gate
  and and_46 (\and , and_34_out, ~in_2[0]);  // AND_Gate
  and and_47 (and_47_out, and_34_out, in_2[0]);
  and and_48 (\nor , and_47_out, in_2[1]);
  and and_49 (\or , ~in_2[1], and_47_out);  // AND_Gate
  and and_50 (halt, in_2[0], Especial, in_2[1]);
  and and_51 (tty, in_2[0], Especial, ~in_2[1]);  // AND_Gate
  and and_52 (rnd, ~in_2[0], Especial, in_2[1]);  // AND_Gate
  and and_53 (kbd, ~in_2[0], Especial, ~in_2[1]);  // AND_Gate

  // Other names for the same wires on the sheet: F_bit1 = in_2[0]; FuncCode[5:0] = in_2; F_bit2 = in_2[1];
  //   F_bit3 = in_2[2]; F_bit4 = in_2[3]; OpCode[5:0] = in_1; Bit3 = in_1[2]; Bit4 = in_1[3]; Bit6 = in_1[5]

  // Notes on the sheet:
  //   Tipo R
endmodule

module TYPE_AL (
  input  Inputs,
  input  in_2,
  input  in_3,
  input  in_4,
  input  in_5,
  input  in_6,
  input  in_7,
  input  in_8,
  input  in_9,
  input  in_10,
  input  in_11,
  input  in_12,
  input  in_13,
  input  in_14,
  input  in_15,
  input  in_16,
  input  in_17,
  output out_18,
  output out_19,
  output [2:0] out_20,
  output out_21,
  output [2:0] out_22,
  output [1:0] out_23
);

  wire not_1_out, or_5_out, or_6_out, or_7_out, or_8_out;
  wire [1:0] or_4_out;
  wire [2:0] or_1_out;

  or or_1 (or_1_out[0], in_6, in_3, in_5, in_11, in_9, in_13);
  or or_2 (or_1_out[1], in_13, in_4, in_5, in_8, in_9, in_12);
  or or_3 (or_1_out[2], in_7, in_8, in_6, in_9);
  and and_1 (or_4_out[1], in_15, not_1_out);
  not not_1 (not_1_out, in_14);
  or or_4 (or_4_out[0], in_15, in_14);
  or or_5 (or_5_out, in_2, or_6_out);
  or or_6 (or_6_out, or_1_out[0], or_1_out[1], or_1_out[2]);
  assign out_20 = or_1_out & {3{Inputs}};  // AND_Gate and_2, 3 bits wide
  assign out_22 = {in_14, or_4_out} & {3{Inputs}};  // AND_Gate and_3, 3 bits wide
  assign out_23 = {in_16, 1'b0} & {2{Inputs}};  // AND_Gate and_4, 2 bits wide
  or or_7 (or_7_out, in_10, in_11, in_12, in_13);
  or or_8 (or_8_out, or_5_out, in_14, in_15);
  and and_5 (out_21, or_7_out, Inputs);
  and and_6 (out_18, or_8_out, ~in_11, ~in_12, ~in_13, Inputs);  // AND_Gate

  assign out_19 = Inputs;

  // Other names for the same wires on the sheet: jr = in_16; mfhi = in_14; EN = Inputs; PC = Inputs; add = in_2;
  //   and = in_4; div = in_12; divu = in_13; LH = out_21; mflo = in_15; mul = in_10; mulu = in_11; nop = in_17;
  //   nor = in_7; or = in_5; Rf_Rw = out_18; S_ALU[2:0] = out_20; S_BC[1:0] = out_23; S_Di[2:0] = out_22; slt = in_8;
  //   sltu = in_9; sub = in_3; xor = in_6

  // Notes on the sheet:
  //   Outputs:
endmodule

module TYPE_INM (
  input  Inputs,
  input  in_2,
  input  in_3,
  input  in_4,
  input  in_5,
  input  in_6,
  input  in_7,
  output [1:0] Outputs,
  output out_9,
  output out_10,
  output [2:0] out_11,
  output out_12
);

  wire or_2_out, or_3_out;
  wire [0:0] or_1_out;
  wire [2:0] or_5_out;

  or or_1 (or_1_out[0], in_2, in_3, in_4, in_5, in_6, in_7);
  and and_1 (out_12, or_1_out[0], Inputs);
  or or_2 (or_2_out, in_4, in_7);
  or or_3 (or_3_out, in_6, in_3);
  or or_4 (or_5_out[2], in_7, in_6, in_5);
  assign Outputs = {1'b0, or_1_out[0]} & {2{Inputs}};  // AND_Gate and_2, 2 bits wide
  or or_5 (or_5_out[0], in_5, or_2_out);
  or or_6 (or_5_out[1], or_2_out, or_3_out);
  assign out_11 = or_5_out & {3{Inputs}};  // AND_Gate and_3, 3 bits wide

  assign out_9 = Inputs;
  assign out_10 = Inputs;

  // Other names for the same wires on the sheet: En = Inputs; PC = Inputs; RW_RF = Inputs; addi = in_2; andi = in_3;
  //   ori = in_4; S_ALU[2:0] = out_11; S_B[1:0] = Outputs; S_DA = out_12; slti = in_6; sltiu = in_7; xori = in_5
endmodule

module TYPE_BRANCH (
  input  Inputs,
  input  in_2,
  input  in_3,
  input  in_4,
  input  in_5,
  input  in_6,
  input  in_7,
  output out_8,
  output [2:0] out_9,
  output [1:0] out_10,
  output [2:0] out_11
);

  wire [0:0] or_1_out, or_2_out;
  wire [2:0] or_4_out;

  or or_1 (or_1_out[0], in_2, in_3, in_4, in_5, in_6);
  or or_2 (or_2_out[0], or_1_out[0], in_7);
  or or_3 (or_4_out[2], in_6, in_5);
  nor nor_1 (or_4_out[1], in_2, in_4);
  or or_4 (or_4_out[0], in_4, in_5);
  assign out_10 = {in_7, or_2_out[0]} & {2{Inputs}};  // AND_Gate and_1, 2 bits wide
  assign out_11 = or_4_out & {3{Inputs}};  // AND_Gate and_2, 3 bits wide
  assign out_9 = {2'b00, or_1_out[0]} & {3{Inputs}};  // AND_Gate and_3, 3 bits wide

  assign out_8 = Inputs;

  // Other names for the same wires on the sheet: jmp = in_7; EN = Inputs; PC = Inputs; beq = in_2; bgtz = in_5;
  //   blez = in_4; bltz = in_6; bne = in_3; S_ALU[2:0] = out_9; S_BC[1:0] = out_10; S_flags[2:0] = out_11

  // Notes on the sheet:
  //   Outputs:
endmodule

module TYPE_WORD (
  input  Inputs,
  input  in_2,
  input  in_3,
  input  in_4,
  input  in_5,
  output out_6,
  output out_7,
  output out_8,
  output out_9,
  output [2:0] out_10,
  output out_11,
  output [1:0] out_12,
  output [1:0] out_13,
  output out_14
);

  wire d_ff_1_q, d_ff_2_q, demultiplexer_1_out0, demultiplexer_2_out0, EndLW, EndSW, PCs, S_Adr0l, startRaml,
       startRams;

  and and_1 (startRaml, in_3, in_2);
  D_Flip_Flop d_ff_1 (.clk(Inputs), .D(demultiplexer_1_out0), .Q(d_ff_1_q));  // open: Qn, preset, en, reset
  and and_2 (startRams, in_3, in_5);
  D_Flip_Flop d_ff_2 (.clk(Inputs), .D(demultiplexer_2_out0), .Q(d_ff_2_q));  // open: Qn, preset, en, reset
  or or_1 (S_Adr0l, startRaml, d_ff_1_q);
  or or_2 (out_7, startRams, d_ff_2_q);
  Demultiplexer #(.enable("false")) demultiplexer_1 (
    .out0(demultiplexer_1_out0), .out1(out_8), .in(S_Adr0l), .sel(in_4));
  Demultiplexer #(.enable("false")) demultiplexer_2 (.out0(demultiplexer_2_out0), .out1(PCs), .in(out_7), .sel(in_4));
  or or_3 (out_11, EndLW, EndSW);
  or or_4 (out_6, startRaml, startRams);
  D_Flip_Flop d_ff_3 (.clk(Inputs), .D(PCs), .Q(EndSW));  // open: Qn, preset, en, reset
  D_Flip_Flop d_ff_4 (.clk(Inputs), .D(out_8), .Q(EndLW));  // open: Qn, preset, en, reset
  or or_5 (out_12[0], out_7, S_Adr0l);
  or or_6 (out_13[0], S_Adr0l, out_7);
  or or_7 (out_14, out_8, PCs);

  assign out_9 = out_8;
  assign out_10 = {2'b00, out_8};
  assign out_12[1] = 1'b0;
  assign out_13[1] = 1'b0;

  // Other names for the same wires on the sheet: Clk = Inputs; EN = in_3; ENDw = out_11; LoadWord = in_2; PC = out_14;
  //   RamReady = in_4; S_Adr[0] = out_13[0]; S_B[0] = out_12[0]; S_B0l = S_Adr0l; RamW = out_7; S_Adr0s = out_7;
  //   S_B0s = out_7; PCl = out_8; Rf_Rw = out_8; S_DA = out_8; S_Di[0] = out_8; S_Di0 = out_8; startRam = out_6;
  //   StoreWord = in_5

  // Notes on the sheet:
  //   Load:
  //   Store:
  //   Outputs:
endmodule

module TYPE_SPECIAL (
  input  Inputs,
  input  in_2,
  input  in_3,
  input  in_4,
  output out_5,
  output [2:0] out_6,
  output out_7,
  output out_8,
  output out_9
);

  wire [2:2] or_1_out;

  and and_1 (out_9, in_4, Inputs);
  or or_1 (or_1_out[2], in_2, in_3);
  and and_2 (out_5, or_1_out[2], Inputs);
  assign out_6 = {{2{or_1_out[2]}}, in_2} & {3{Inputs}};  // AND_Gate and_3, 3 bits wide
  and and_4 (out_7, in_2, Inputs);

  assign out_8 = Inputs;

  // Other names for the same wires on the sheet: kbd = in_2; En = Inputs; PC = Inputs; kbdEn = out_7; Rf = out_5;
  //   rnd = in_3; S_Di[2:0] = out_6; tty = in_4; tty_Enable = out_9

  // Notes on the sheet:
  //   Outputs:
endmodule

module TYPE_STACK (
  input  in_1,
  input  in_2,
  input  in_3,
  input  in_4,
  input  in_5,
  output out_6,
  output out_7,
  output out_8,
  output [1:0] out_9,
  output [1:0] out_10,
  output out_11,
  output [2:0] out_12,
  output out_13,
  output out_14,
  output out_15,
  output out_16,
  output [2:0] out_17
);

  wire d_ff_1_q, d_ff_3_q, demultiplexer_1_out0, demultiplexer_2_out0, EndPop, EndPush, PCpush, S_Adr1pop,
       startRampop, startRampush;

  and and_1 (startRampop, in_3, in_1);
  or or_1 (S_Adr1pop, startRampop, d_ff_1_q);
  D_Flip_Flop d_ff_1 (.clk(in_5), .D(demultiplexer_1_out0), .Q(d_ff_1_q));  // open: Qn, preset, en, reset
  and and_2 (out_12[0], in_3, in_2);
  or or_2 (out_8, out_7, out_12[0]);
  or or_3 (out_10[1], out_7, out_12[0]);
  Demultiplexer #(.enable("false")) demultiplexer_1 (
    .out0(demultiplexer_1_out0), .out1(out_7), .in(S_Adr1pop), .sel(in_4));
  or or_4 (out_9[1], S_Adr1pop, out_14);
  or or_5 (out_13, out_7, out_12[0]);
  D_Flip_Flop d_ff_2 (.clk(in_5), .D(out_12[0]), .Q(startRampush));  // open: Qn, preset, en, reset
  D_Flip_Flop d_ff_3 (.clk(in_5), .D(demultiplexer_2_out0), .Q(d_ff_3_q));  // open: Qn, preset, en, reset
  or or_6 (out_14, startRampush, d_ff_3_q);
  or or_7 (out_11, out_7, PCpush);
  D_Flip_Flop d_ff_4 (.clk(in_5), .D(out_7), .Q(EndPop));  // open: Qn, preset, en, reset
  or or_8 (out_16, startRampop, startRampush);
  Demultiplexer #(.enable("false")) demultiplexer_2 (
    .out0(demultiplexer_2_out0), .out1(PCpush), .in(out_14), .sel(in_4));
  or or_9 (out_6, EndPop, EndPush);
  D_Flip_Flop d_ff_5 (.clk(in_5), .D(PCpush), .Q(EndPush));  // open: Qn, preset, en, reset

  assign out_9[0] = 1'b0;
  assign out_10[0] = out_10[1];
  assign out_12[2:1] = 2'b00;
  assign out_15 = out_14;
  assign out_17 = {2'b00, out_7};

  // Other names for the same wires on the sheet: Clk = in_5; En = in_3; ENDStack = out_6; PC = out_11; pop = in_1;
  //   push = in_2; RamReady = in_4; S_A = out_8; S_Adr[1] = out_9[1]; S_ALU[0] = out_12[0]; S_ALU0 = out_12[0];
  //   S_Apush = out_12[0]; S_Bpush = out_12[0]; SP_RWpush = out_12[0]; S_B[1:0] = {2{out_10[1]}}; PCpop = out_7;
  //   Rf_Rw = out_7; S_Apop = out_7; S_Bpop = out_7; S_Di[0] = out_7; S_Di0 = out_7; SP_RWpop = out_7; RamW = out_14;
  //   S_Adr1push = out_14; S_Do = out_14; SP_RW = out_13; startRam = out_16

  // Notes on the sheet:
  //   Inputs:
  //   Pop:
  //   Push:
  //   Outputs:
endmodule

module RamManager (
  input  [31:0] Addres_In,
  input  [31:0] Ram_out_0,
  input  [31:0] Ram_out_1,
  input  [31:0] Ram_out_2,
  input  [31:0] Ram_out_3,
  input  [3:0] Read_Time,
  input  Clk,
  input  Rst,
  input  [3:0] Write_Time,
  input  Start,
  input  R_W,
  output [31:0] From_RAM,
  output [3:0] Mask,
  output [15:0] ADDR,
  output RAMReady,
  output Chip_Select,
  output RAM_Write,
  output [1:0] Bank
);

  wire Clear, comparator_1_lt, demultiplexer_1_out0, IsFetch, or_1_out, Wait_q;
  wire [3:0] counter_1_q, Time;
  wire [31:0] multiplexer_2_out;

  Multiplexer #(.width(4), .enable("false")) multiplexer_1 (.in0(Read_Time), .in1(Write_Time), .out(Time), .sel(R_W));
  D_Flip_Flop #(.trigger("falling")) Wait (
    .clk(Clk), .D(demultiplexer_1_out0), .Q(Wait_q));  // open: Qn, preset, en, reset
  Counter #(.width(4), .max('hf), .trigger("falling")) counter_1 (
    .count(Chip_Select), .Q(counter_1_q), .clk(Clk), .clr(or_1_out));  // open: load, D, carry
  or or_1 (or_1_out, Rst, Clear);
  or or_2 (Chip_Select, Wait_q, Start);
  Demultiplexer #(.enable("false")) demultiplexer_1 (
    .out0(demultiplexer_1_out0), .out1(RAMReady), .in(Chip_Select), .sel(IsFetch));
  Comparator #(.width(4), .mode("unsigned")) comparator_1 (
    .a(counter_1_q), .b(Time), .lt(comparator_1_lt));  // open: gt, eq
  not not_1 (IsFetch, comparator_1_lt);
  D_Flip_Flop End (.clk(Clk), .D(RAMReady), .Q(Clear));  // open: Qn, preset, en, reset
  Multiplexer #(.select(2), .width(32), .enable("false")) multiplexer_2 (
    .in0(Ram_out_0), .in1(Ram_out_1), .in2(Ram_out_2), .in3(Ram_out_3), .out(multiplexer_2_out),
    .sel(Addres_In[1:0]));
  Decoder #(.select(2), .enable("false")) decoder_1 (
    .out0(Mask[0]), .out1(Mask[1]), .out2(Mask[2]), .out3(Mask[3]), .sel(Addres_In[1:0]));
  LittleEndianSwap littleendianswap_1 (.Input(multiplexer_2_out), .Output(From_RAM));
  and and_1 (RAM_Write, R_W, Chip_Select);

  assign ADDR = Addres_In[17:2];
  assign Bank = Addres_In[1:0];

  // Other names for the same wires on the sheet: Block[15:0] = Addres_In[17:2]; End = RAMReady; Count = Chip_Select;
  //   CS = Chip_Select; RAM_Wr = Chip_Select; RW = R_W

  // Notes on the sheet:
  //   ADDRESS
  //   DATA FROM RAM
  //   RAM TIMING
  //   CONTROL SIGNALS
  //   TIMER
  //   FLOW CONTROL
endmodule

module LittleEndianSwap (
  input  [31:0] Input,
  output [31:0] Output
);


  assign Output = {Input[7:0], Input[15:8], Input[23:16], Input[31:24]};
endmodule
